# Fritzing sketch single-sr (saved by Fritzing 0.9.3b)
breadboards: 1

parts:
  Part1 = Arduino Uno (Rev3)
  U1 = 74HC595 [package="DIP16 [THT]"]

nets:
  GND: Part1.GND, U1.GND, U1.OE
  N1: Part1.D2, U1.DS
  N2: Part1.D3_PWM, U1.SH_CP
  N3: Part1.D4, U1.ST_CP
  5V: Part1.5V, U1.MR, U1.VCC
